# Fritzing sketch Diagrama_SIM800L (saved by Fritzing 0.9.3b)
breadboards: 2

parts:
  SIM800L_BO1 = SIM800L BO
  Part1 = Arduino Uno (Rev3)

nets:
  N1: SIM800L_BO1.PIN2, Part1.5V
  N2: SIM800L_BO1.pin_4, Part1.D3_PWM
  N3: SIM800L_BO1.pin_5, Part1.D2
  N4: SIM800L_BO1.pin_6, Part1.GND
